// Logisim project Basic Computer.circ as structural Verilog: 3 circuits, main circuit main
module main (
  input  in_1,
  output E
);

  wire ACL, ARL, clock_1_out, DRL, IRL, MR, MW, PCinc, PCL;
  wire [2:0] control_unit_1_alu_selection, control_unit_1_bus_selection;
  wire [6:0] AR_q, bit_extender_1_out;
  wire [15:0] AC_q, alu_1_ac_output, bit_extender_2_out, DR_q, IR_q, multiplexer_1_out, PC_q, ram_1_data,
       TR_q;

  Bit_Extender #(.in_width(16), .out_width(7)) bit_extender_1 (.in(multiplexer_1_out), .out(bit_extender_1_out));
  Clock clock_1 (.out(clock_1_out));
  Register #(.width(7)) AR (.D(bit_extender_1_out), .en(ARL), .Q(AR_q), .clk(clock_1_out));  // open: clr
  Register #(.width(16)) TR (.D(multiplexer_1_out), .en(in_1), .Q(TR_q), .clk(clock_1_out));  // open: clr
  Register #(.width(16)) DR (.D(multiplexer_1_out), .en(DRL), .Q(DR_q), .clk(clock_1_out));  // open: clr
  Register #(.width(16)) AC (.D(alu_1_ac_output), .en(ACL), .Q(AC_q), .clk(clock_1_out));  // open: clr
  Counter #(.width(16), .max('hffff)) PC (
    .load(PCL), .D(multiplexer_1_out), .count(PCinc), .Q(PC_q), .clk(clock_1_out));  // open: carry, clr
  Register #(.width(16)) IR (.D(multiplexer_1_out), .en(IRL), .Q(IR_q), .clk(clock_1_out));  // open: clr
  RAM #(.addrWidth(7), .dataWidth(16), .bus("separate")) ram_1 (
    .addr(AR_q), .din(multiplexer_1_out), .data(ram_1_data), .str(MW), .clk(clock_1_out), .ld(MR));  // open: sel, clr
  assign bit_extender_2_out = {{9{1'b0}}, AR_q};  // Bit_Extender bit_extender_2
  ALU alu_1 (.A(DR_q), .B(AC_q), .in_3(control_unit_1_alu_selection), .E(E), .AC_Output(alu_1_ac_output));
  Control_Unit control_unit_1 (
    .IR(IR_q), .Clock(clock_1_out), .AC(AC_q), .ARL(ARL), .PCinc(PCinc),
    .Bus_Selection(control_unit_1_bus_selection), .MR(MR), .MW(MW), .ACL(ACL), .DRL(DRL),
    .ALU_Selection(control_unit_1_alu_selection), .IRL(IRL), .PCL(PCL));
  Multiplexer #(.select(3), .width(16)) multiplexer_1 (
    .in0(ram_1_data), .in1(bit_extender_2_out), .in2(TR_q), .in3(DR_q), .in4(AC_q), .in5(PC_q), .in6(IR_q),
    .out(multiplexer_1_out), .sel(control_unit_1_bus_selection));  // open: in7, en
endmodule

module ALU (
  input  [15:0] A,
  input  [15:0] B,
  input  [2:0] in_3,
  output E,
  output [15:0] AC_Output
);

  wire adder_1_cout, adder_2_cout, subtractor_1_bout;
  wire [15:0] adder_1_out, adder_2_out, and_1_out, or_1_out, subtractor_1_out, xor_1_out;

  Adder #(.width(16)) adder_1 (.a(A), .b(B), .out(adder_1_out), .cin(1'b0), .cout(adder_1_cout));
  Subtractor #(.width(16)) subtractor_1 (.a(A), .b(B), .out(subtractor_1_out), .bin(1'b0), .bout(subtractor_1_bout));
  assign and_1_out = A & B;  // AND_Gate and_1, 16 bits wide
  assign or_1_out = A | B;  // OR_Gate or_1, 16 bits wide
  assign xor_1_out = A ^ B;  // XOR_Gate xor_1, 16 bits wide
  Adder #(.width(16)) adder_2 (.a(A), .b({16{1'b0}}), .out(adder_2_out), .cin(1'b1), .cout(adder_2_cout));
  or or_2 (E, adder_1_cout, subtractor_1_bout, adder_2_cout);
  Multiplexer #(.select(3), .width(16)) multiplexer_1 (
    .in1(adder_1_out), .in2(subtractor_1_out), .in3(A), .in4(and_1_out), .in5(or_1_out), .in6(xor_1_out),
    .in7(adder_2_out), .out(AC_Output), .sel(in_3));  // open: in0, en
endmodule

module Control_Unit (
  input  [15:0] IR,
  input  Clock,
  input  [15:0] AC,
  output ARL,
  output PCinc,
  output [2:0] Bus_Selection,
  output MR,
  output MW,
  output ACL,
  output DRL,
  output [2:0] ALU_Selection,
  output IRL,
  output PCL
);

  wire AC_prime, AC_t, and_1_out, D0, D0T4, D0T5, D1, D1T4, D1T5, D2, D2T4, D2T5, D3, D3T4, D4, D5, D5T4,
       D5T5, D5T6, D6, D6T6, D7, D7_prime_IT3, D7I_prime_T3, D7I_prime_T3B2, D7I_prime_T3B5, D7I_prime_T4,
       D7I_prime_T4B5, d_ff_1_q, decoder_2_out7, decoder_2_out8, decoder_2_out9, decoder_2_out10,
       decoder_2_out11, decoder_2_out12, decoder_2_out13, decoder_2_out14, decoder_2_out15, IR_t, not_1_out,
       not_2_out, not_3_out, or_1_out, or_3_out, PC, rB2AC_prime, T3, T4, T5, T6, Transfer;
  wire [3:0] counter_1_q;

  Counter #(.width(4), .max('hf)) counter_1 (
    .count(Clock), .Q(counter_1_q), .clk(Clock), .clr(d_ff_1_q));  // open: load, D, carry
  or or_1 (or_1_out, D2T5, D1T5, D5T6, PCL, D3T4, D0T5, D7I_prime_T3B2, D7I_prime_T4B5);
  Decoder #(.select(3)) decoder_1 (
    .out0(D0), .out1(D1), .out2(D2), .out3(D3), .out4(D4), .out5(D5), .out6(D6), .out7(D7), .sel(IR[14:12]));  // open: en
  Decoder #(.select(4)) decoder_2 (
    .out0(PC), .out1(IRL), .out2(IR_t), .out3(T3), .out4(T4), .out5(T5), .out6(T6), .out7(decoder_2_out7),
    .out8(decoder_2_out8), .out9(decoder_2_out9), .out10(decoder_2_out10), .out11(decoder_2_out11),
    .out12(decoder_2_out12), .out13(decoder_2_out13), .out14(decoder_2_out14), .out15(decoder_2_out15),
    .sel(counter_1_q));  // open: en
  D_Flip_Flop d_ff_1 (.clk(Clock), .D(or_1_out), .Q(d_ff_1_q));  // open: Qn, preset, en, reset
  nor nor_1 (AC_prime, AC[0], AC[1], AC[2], AC[3], AC[4], AC[5], AC[6], AC[7], AC[8], AC[9], AC[10], AC[11], AC[12], AC[13], AC[14], AC[15]);
  Priority_Encoder priority_encoder_1 (
    .in0(MR), .in1(PCL), .in4(AC_t), .in5(PC), .in6(IR_t), .out(Bus_Selection));  // open: in2, in3, in7, en_in, gs, en_out
  Priority_Encoder priority_encoder_2 (
    .in1(D1T5), .in2(D5T6), .in3(Transfer), .in4(D0T5), .in7(D7I_prime_T4B5), .out(ALU_Selection));  // open: in0, in5, in6, en_in, gs, en_out
  or or_2 (ARL, IR_t, PC);
  or or_3 (or_3_out, D5, D2, D1, D0);
  and and_1 (and_1_out, T4, or_3_out);
  or or_4 (MW, D3T4, D5T4);
  or or_5 (MR, and_1_out, IRL);
  or or_6 (ACL, D7I_prime_T4B5, D0T5, D1T5, D2T5, D5T6, D5T5);
  or or_7 (PCinc, IRL, rB2AC_prime);
  or or_8 (AC_t, D7I_prime_T3B5, D3T4, D5T5);
  or or_9 (DRL, D0T4, D1T4, D2T4, D5T5, D5T4, D7I_prime_T3B5);
  and and_2 (D2T5, D2, T5);
  and and_3 (D1T5, D1, T5);
  and and_4 (D5T6, D5, T6);
  and and_5 (PCL, D4, T4);
  and and_6 (D0T5, D0, T5);
  and and_7 (D3T4, D3, T4);
  or or_10 (Transfer, D5T5, D2T5);
  not not_1 (not_1_out, IR[15]);
  and and_8 (D7I_prime_T3, T3, D7, not_1_out);
  and and_9 (D2T4, D2, T4);
  and and_10 (D1T4, D1, T4);
  and and_11 (D5T4, D5, T4);
  and and_12 (D5T5, D5, T5);
  and and_13 (D0T4, D0, T4);
  and and_14 (D7I_prime_T3B5, D7I_prime_T3, IR[5]);
  and and_15 (D7I_prime_T3B2, D7I_prime_T3, IR[2]);
  and and_16 (D7I_prime_T4B5, D7I_prime_T4, IR[5]);
  and and_17 (D6T6, T6, D6);
  not not_2 (not_2_out, D7);
  not not_3 (not_3_out, IR[15]);
  and and_18 (D5T4, T4, D5);
  and and_19 (rB2AC_prime, D7I_prime_T3, IR[2], AC_prime);
  and and_20 (D7_prime_IT3, T3, IR[15], not_2_out);
  and and_21 (D7I_prime_T4, T4, D7, not_3_out);

  // Other names for the same wires on the sheet: AR = PCL; D4T4 = PCL; B0 = IR[0]; B1 = IR[1]; B2 = IR[2]; B3 = IR[3];
  //   B4 = IR[4]; B5 = IR[5]; B6 = IR[6]; B7 = IR[7]; B8 = IR[8]; B9 = IR[9]; B10 = IR[10]; B11 = IR[11]; I = IR[15];
  //   T0 = PC; T1 = IRL; T2 = IR_t
endmodule
